# Fritzing sketch CIRCUIT-SMST (saved by Fritzing 0.9.6b)
circuit board: 20cm x 20cm
breadboards: 1

parts:
  IC1 = AT89S51
  RED4 = LED - 5mm [color="Red (633nm)" current=0.030 package="5 mm [THT]"]
  YELLOW4 = LED - 5mm [color="Yellow (595nm)" current=0.030 package="5 mm [THT]"]
  GREEN4 = LED - 5mm [color="Green (570nm)" current=0.030 package="5 mm [THT]"]
  RED1 = LED - 5mm [color="Red (633nm)" current=0.030 package="5 mm [THT]"]
  YELLOW1 = LED - 5mm [color="Yellow (595nm)" current=0.030 package="5 mm [THT]"]
  GREEN1 = LED - 5mm [color="Green (570nm)" current=0.030 package="5 mm [THT]"]
  RED2 = LED - 5mm [color="Red (633nm)" current=0.030 package="5 mm [THT]"]
  YELLOW2 = LED - 5mm [color="Yellow (595nm)" current=0.030 package="5 mm [THT]"]
  GREEN2 = LED - 5mm [color="Green (570nm)" current=0.030 package="5 mm [THT]"]
  RED3 = LED - 5mm [color="Red (633nm)" current=0.030 package="5 mm [THT]"]
  YELLOW3 = LED - 5mm [color="Yellow (595nm)" current=0.030 package="5 mm [THT]"]
  GREEN3 = LED - 5mm [color="Green (570nm)" current=0.030 package="5 mm [THT]"]
  WeMos_D1_Mini1 = WeMos D1 Mini
  C1 = Capacitor [part_number=33p package=cap-pth-small2]
  C2 = Capacitor [part_number=33p package=cap-pth-small2]
  M1 = fc-51 [package=THT]
  M2 = fc-51 [package=THT]
  M3 = fc-51 [package=THT]
  M4 = fc-51 [package=THT]
  M5 = fc-51 [package=THT]
  M6 = fc-51 [package=THT]
  M7 = fc-51 [package=THT]
  M8 = fc-51 [package=THT]
  B1 = LED - 5mm [color="Blue (505nm)" current=0.030 package="5 mm [THT]"]
  B2 = LED - 5mm [color="Blue (505nm)" current=0.030 package="5 mm [THT]"]
  B3 = LED - 5mm [color="Blue (505nm)" current=0.030 package="5 mm [THT]"]
  B4 = LED - 5mm [color="Blue (505nm)" current=0.030 package="5 mm [THT]"]
  R1 = Resistor [tolerance=±5% power=0.25 resistance=220 package=THT]
  R2 = 8 Resistor Network [part_number=4.7kΩ package="SIP (Single Inline)"]
  R2_1 = 8 Resistor Network [part_number=4.7kΩ package="SIP (Single Inline)"]
  R2_2 = 8 Resistor Network [part_number=4.7kΩ package="SIP (Single Inline)"]
  R2_3 = 8 Resistor Network [part_number=4.7kΩ package="SIP (Single Inline)"]
  R2_4 = 8 Resistor Network [part_number=4.7kΩ package="SIP (Single Inline)"]
  R2_5 = 8 Resistor Network [part_number=4.7kΩ package="SIP (Single Inline)"]
  R2_6 = 8 Resistor Network [part_number=4.7kΩ package="SIP (Single Inline)"]
  R2_7 = 8 Resistor Network [part_number=4.7kΩ package="SIP (Single Inline)"]
  R2_8 = 8 Resistor Network [part_number=4.7kΩ package="SIP (Single Inline)"]
  Y1 = CRYSTAL [package=hc49u-v]

nets:
  N1: IC1.P1.0_(T2), WeMos_D1_Mini1.D1
  N2: IC1.P1.1_(T2EX), WeMos_D1_Mini1.D2
  N3: IC1.P1.2, WeMos_D1_Mini1.D3
  N4: IC1.P1.3, WeMos_D1_Mini1.D4
  N5: IC1.P3.2_(~INT0), IC1.~EA/VPP, RED2.anode
  N6: IC1.P3.3_(~INT1), YELLOW2.anode
  N7: IC1.P3.4_(T0), GREEN2.anode
  N8: IC1.P3.5_(T1), RED3.anode
  N9: IC1.P3.6_(~WR), YELLOW3.anode
  N10: IC1.P3.7_(~RD), GREEN3.anode
  N11: IC1.XTAL2, C2.1, Y1.1
  N12: IC1.XTAL1, C1.1, Y1.2
  GND: IC1.GND, RED4.cathode, YELLOW4.cathode, GREEN4.cathode, RED1.cathode, YELLOW1.cathode, GREEN1.cathode, RED2.cathode, YELLOW2.cathode, GREEN2.cathode, RED3.cathode, YELLOW3.cathode, GREEN3.cathode, WeMos_D1_Mini1.G, C1.2, C2.2, M1.pin2, M2.pin2, M3.pin2, M4.pin2, M5.pin2, M6.pin2, M7.pin2, M8.pin2, R1.Pin_0
  N13: IC1.P2.2_(A10), GREEN1.anode
  N14: IC1.P2.3_(A11), YELLOW1.anode
  N15: IC1.P2.4_(A12), RED1.anode
  N16: IC1.P2.5_(A13), GREEN4.anode
  N17: IC1.P2.6_(A14), YELLOW4.anode
  N18: IC1.P2.7_(A15), RED4.anode
  N19: IC1.P0.7_(AD7), M8.pin1, R2.connector8, R2_8.9
  N20: IC1.P0.6_(AD6), M7.pin1, R2.connector7, R2_7.8
  N21: IC1.P0.5_(AD5), M6.pin1, R2.connector6, R2_6.7
  N22: IC1.P0.4_(AD4), M5.pin1, R2.connector5, R2_5.6
  N23: IC1.P0.3_(AD3), M4.pin1, R2.connector4, R2_4.5
  N24: IC1.P0.2_(AD2), M3.pin1, R2_3.4
  N25: IC1.P0.1_(AD1), M2.pin1, R2.connector2, R2_2.3
  N26: IC1.P0.0_(AD0), M1.pin1, R2.connector1, R2_1.2
  N27: IC1.VCC, M1.pin3, M2.pin3, M3.pin3, M4.pin3, M5.pin3, M6.pin3, M7.pin3, M8.pin3, R2.connector12, R2_1.11
  N28: WeMos_D1_Mini1.D5, B1.anode
  N29: WeMos_D1_Mini1.D6, B2.anode
  N30: WeMos_D1_Mini1.D7, B3.anode
  N31: WeMos_D1_Mini1.D8, B4.anode
  N32: B1.cathode, B2.cathode, B3.cathode, B4.cathode, R1.Pin_1

custom parts:
  AT89S51: AT89S51 DIP40 from Atmel
